// Logisim project Lesson1.circ as structural Verilog
module main (
  input  in_1,
  input  in_2
);

  wire j_and_1_out1;

  LED led_1 (.in(j_and_1_out1));
  j_and j_and_1 (.in1(in_1), .in2(in_2), .out1(j_and_1_out1));
endmodule

// VHDL entity j_and, as the project stores it:
LIBRARY ieee;
USE ieee.std_logic_1164.all;

ENTITY j_and IS
  PORT (
  --Input----------------------------------------------------------------------------
    in1: IN std_logic;
    in2: IN std_logic;
  --Output----------------------------------------------------------------------------
    out1: OUT std_logic
    );
    
END j_and;


ARCHITECTURE TypeArchitecture OF j_and IS

BEGIN
	out1 <= in1;

END TypeArchitecture;
